# Fritzing sketch TP-FINAL (saved by Fritzing 1.0.6)
breadboards: 1

parts:
  Componente2 = Arduino Mega 2560 (Rev3)
  A1 = ESP01S Adaptor [package="DIP (Dual Inline) [THT]"]
  U1 = ESP8266 WiFi Module [part_number=ESP8266]
  Componente3 = sensor_biometrico
  Grove1 = Grove RGB LCD
  Componente5 = RFID-RC522-v3
  J1 = Piezo Speaker
  S1 = Pushbutton [package="[SMD]"]
  Mod1 = YL-99 Limit switch and LED
  Mod2 = YL-99 Limit switch and LED

nets:
  N1: Componente2.D21/SCL, Grove1.SCL
  N2: Componente2.D20/SDA, Grove1.SDA
  N3: Componente2.D17_PWM/RX2, Componente3.TX
  N4: Componente2.D16_PWM/TX2, Componente3.RX
  N5: Componente2.D15/RX3, A1.TX#1
  N6: Componente2.D14/TX3, A1.RX#0
  GND: Componente2.GND, A1.GND#3, Componente3.GND, Grove1.GND, Componente5.GND, J1.pin1, S1.Pin_3, S1.Pin_4, Mod1.GND, Mod2.GND
  3V3: Componente2.3V3, Componente5.3.3V
  VCC: Componente2.5V, A1.VCC, Componente3.VCC, Grove1.VCC
  N7: Componente2.D5_PWM, Componente5.RST
  N8: Componente2.D7_PWM, J1.pin2
  N9: Componente2.D25, Mod2.OUT
  N10: Componente2.D26, Mod1.OUT
  N11: Componente2.D48, S1.Pin_1, S1.Pin_2
  N12: Componente2.D50, Componente5.MISO
  N13: Componente2.D51, Componente5.MOSI
  N14: Componente2.D52, Componente5.SCK
  N15: Componente2.D53, Componente5.SDA
  N16: A1.TX#4, U1.TXD
  N17: A1.EN, U1.CH_PD
  N18: A1.RST, U1.RST
  3V3_2: A1.3V3, U1.VCC
  N19: A1.RX#8, U1.RXD
  N20: A1.IO0, U1.GPIO_0
  N21: A1.IO2, U1.GPIO_2
  N22: A1.GND#11, U1.GND

custom parts:
  ESP01S Adaptor: Please ignore the PCB view — it's not supposed to be there.
  ESP8266 WiFi Module: Generic WiFi Module based on the ESP8266 with onboard PCB antenna and UART communications
  sensor_biometrico: Adafruit Optical Fingerprint Sensor
  RFID-RC522-v3: A simple China made RFID-RC522 Reader (6x4 cm); do check the pin labels, as this is a MFRC522 based clone.
